# Fritzing sketch Cat Feeder Diagram Backup (saved by Fritzing 0.9.2b)
breadboards: 1

parts:
  Parallax_RFID_Read/Write_125_kHz = Header 4 [part_number=28440 package=1x04-smd]
  Door_Motor = Stepper Motor - Bipolar
  EDGY_motor_control_Door_Motor_Controller_(Bidirectional) = EDGY
  Power_plug1 = Power plug
  Raspberry_Pi1 = Raspberry Pi 2
  Food_aggetator = Basic Servo
  Door_Sensor_-_Textile_Resistor_(Flex) = Textile Stretch Sensor [part_number=PW052]
  R2 = Resistor [tolerance=±5% resistance=22 package="2010 [SMD]"]  # not connected
  Weight_Textile_Resistor = Textile Analog Pressure Sensor

nets:
  5V: Parallax_RFID_Read/Write_125_kHz.1, EDGY_motor_control_Door_Motor_Controller_(Bidirectional).5V+, Raspberry_Pi1.5V, Food_aggetator.vcc, Door_Sensor_-_Textile_Resistor_(Flex).pin_0
  GND: Parallax_RFID_Read/Write_125_kHz.4, EDGY_motor_control_Door_Motor_Controller_(Bidirectional).GND, Power_plug1.GND, Raspberry_Pi1.GND, Food_aggetator.gnd, Weight_Textile_Resistor.pin_1
  N1: Door_Motor.A, EDGY_motor_control_Door_Motor_Controller_(Bidirectional).A1out
  N2: Door_Motor.C, EDGY_motor_control_Door_Motor_Controller_(Bidirectional).B1out
  N3: Door_Motor.B, EDGY_motor_control_Door_Motor_Controller_(Bidirectional).A2out
  N4: Door_Motor.D, EDGY_motor_control_Door_Motor_Controller_(Bidirectional).B2out
  N5: EDGY_motor_control_Door_Motor_Controller_(Bidirectional).A1, Raspberry_Pi1.GPIO25
  N6: EDGY_motor_control_Door_Motor_Controller_(Bidirectional).B1, Raspberry_Pi1.GPIO5
  N7: EDGY_motor_control_Door_Motor_Controller_(Bidirectional).Speed1, Raspberry_Pi1.GPIO6
  VIN: EDGY_motor_control_Door_Motor_Controller_(Bidirectional).Vin, Power_plug1.VCC
  N8: EDGY_motor_control_Door_Motor_Controller_(Bidirectional).A2, Raspberry_Pi1.GPIO13
  N9: EDGY_motor_control_Door_Motor_Controller_(Bidirectional).B2, Raspberry_Pi1.GPIO16
  N10: EDGY_motor_control_Door_Motor_Controller_(Bidirectional).Speed2, Raspberry_Pi1.GPIO26
  N11: Raspberry_Pi1.GPIO4, Food_aggetator.pulse
  N12: Raspberry_Pi1.GPIO17, Door_Sensor_-_Textile_Resistor_(Flex).pin_1
