# Fritzing sketch Cat Feeder Diagram Stepper Integrated Electronics (saved by Fritzing 0.9.2b)
circuit board: 20.9484cm x 13.2497cm
breadboards: 1

parts:
  Parallax_RFID_Read/Write_125_kHz = Header 4 [part_number=28440 package=1x04-smd]
  Door_Motor = Stepper Motor - Bipolar
  Power_plug1 = Power plug
  Raspberry_Pi1 = Raspberry Pi 2
  Food_aggetator = Basic Servo
  Door_Sensor_-_Textile_Resistor_(Flex) = Textile Stretch Sensor [part_number=PW052]
  R2 = Resistor [tolerance=±5% resistance=22 package="2010 [SMD]"]
  Weight_Textile_Resistor = Textile Analog Pressure Sensor [part_number=PW073]
  Part1 = EasyDriver_v44
  R3 = Resistor [tolerance=±5% resistance=22 package="2010 [SMD]"]
  S1 = Round Pushbutton
  R4 = Resistor [tolerance=±5% resistance=22 package="2010 [SMD]"]

nets:
  5V: Parallax_RFID_Read/Write_125_kHz.1, Raspberry_Pi1.5V, Food_aggetator.vcc, Door_Sensor_-_Textile_Resistor_(Flex).pin_0, S1.leg0
  N1: Parallax_RFID_Read/Write_125_kHz.2, Raspberry_Pi1.GPIO23
  N2: Parallax_RFID_Read/Write_125_kHz.3, Raspberry_Pi1.GPIO24
  GND: Parallax_RFID_Read/Write_125_kHz.4, Raspberry_Pi1.GND, Food_aggetator.gnd, R2.Pin_0, Weight_Textile_Resistor.pin_1, R3.Pin_0, R4.Pin_0
  N3: Door_Motor.A, Part1.OUT2A
  N4: Door_Motor.C, Part1.OUT2B
  N5: Door_Motor.B, Part1.OUT1A
  N6: Door_Motor.D, Part1.OUT1B
  GND_2: Power_plug1.GND, Part1.GND
  N7: Power_plug1.VCC, Part1.V+
  N8: Raspberry_Pi1.GPIO4, Food_aggetator.pulse
  N9: Raspberry_Pi1.GPIO17, Door_Sensor_-_Textile_Resistor_(Flex).pin_1, R3.Pin_1
  N10: Raspberry_Pi1.GPIO27, R2.Pin_1, Weight_Textile_Resistor.pin_0
  N11: Raspberry_Pi1.GPIO5, Part1.MS1, Part1.SLEEP
  N12: Raspberry_Pi1.GPIO6, Part1.STEP
  N13: Raspberry_Pi1.GPIO13, Part1.DIR
  N14: Raspberry_Pi1.GPIO26, S1.leg1, R4.Pin_1
  N15: Raspberry_Pi1.GPIO20, Part1.ENABLE
  N16: Raspberry_Pi1.GPIO25, Part1.MS2
